# Fritzing sketch capG12 (saved by Fritzing 1.0.4)

parts:
  KY1 = KY-038 Sound Sensor Module
  AM1 = AM2320 Humidity and Temperature Sensor [part_number="Adafruit #3721"]
  Part1 = Adafruit MiCS-5524 Gas Sensor [part_number="Adafruit #3199"]
  buz1 = Piezo Buzzer
  LED1 = smd LED [color="Red (633nm)" package="1206 [SMD]"]
  R1 = Photocell (LDR) [power=0.25W dark_resistance_@0.01lx=300kΩ light_resistance_@100lx=400Ω luminance=10lx package=THT]
  R2 = Resistor [tolerance=±5% power=0.25W resistance=8.2k package=THT]
  U1 = LuaNode32 / ESP32 [part_number=ESP32S-PIN30]

nets:
  N1: KY1.AO, U1.D34
  GND: KY1.G, AM1.GND, Part1.GND, Part1.ENABLE, buz1.pin_2, LED1.cathode, R2.Pin_1, U1.GND
  VCC: KY1.VCC, AM1.VDD, R1.pin_0, U1.3V3
  N2: AM1.SDA, U1.D21
  N3: AM1.SCL, U1.D22
  N4: Part1.5.0V, U1.Vin
  N5: Part1.AOUT, U1.D35
  N6: buz1.pin_1, U1.D19
  N7: LED1.anode, U1.D18
  N8: R1.pin_1, R2.Pin_0, U1.D32

custom parts:
  AM2320 Humidity and Temperature Sensor: AM2320 I2C Humidity and Temperature Sensor
  Adafruit MiCS-5524 Gas Sensor: Give your next sensor project a nose for gasses with the Adafruit MiCS-5524 Gas Sensor Breakout. This breakout makes it easy to use this nice sensor from SGX Sensortech. The MiCS-5524 is a robust MEMS sensor for indoor carbon monoxide and natural gas leakage detection, it's suitable also for indoor air quality monitoring; breath checker and early fire detection. Please note: This sensor is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
  Piezo Buzzer: Part from https://www.nutsvolts.com/magazine/article/november2012_SmileysWorkshop modified to be .3 in spacing to match the adafruit buzzer 5V breadboard friendly part.
  LuaNode32 / ESP32: New Image for LuaNode32 DOIT ESP32 DEVKIT V1. Base parts from LuaNode32 / ESP32 ESP32 based LuaNode32 by G.Noorlander DOIT Esp32 DevKit v1 (30 pins long, 11 pins width) by Werner Rothschopf (modified by vanepp Dec 2018)
